// Logisim project minutes_seconds2.circ as structural Verilog: 1 circuit, main circuit main
module main (
  input  in_1,
  input  in_2,
  input  in_3,
  input  in_4,
  input  in_5,
  input  in_6,
  input  in_7,
  input  in_8,
  input  in_9,
  input  in_10,
  input  in_11,
  input  in_12,
  input  in_13,
  input  in_14,
  input  in_15,
  input  in_16,
  input  in_17,
  input  in_18,
  input  in_19,
  input  in_20
);

  wire and_1_out, and_2_out, and_3_out, and_4_out, bcd_to_7_segment_decoder_1_p1,
       bcd_to_7_segment_decoder_1_p2, bcd_to_7_segment_decoder_1_p3, bcd_to_7_segment_decoder_1_p4,
       bcd_to_7_segment_decoder_1_p6, bcd_to_7_segment_decoder_1_p7, bcd_to_7_segment_decoder_1_p8,
       bcd_to_7_segment_decoder_2_p1, bcd_to_7_segment_decoder_2_p2, bcd_to_7_segment_decoder_2_p3,
       bcd_to_7_segment_decoder_2_p4, bcd_to_7_segment_decoder_2_p6, bcd_to_7_segment_decoder_2_p7,
       bcd_to_7_segment_decoder_2_p8, bcd_to_7_segment_decoder_3_p1, bcd_to_7_segment_decoder_3_p2,
       bcd_to_7_segment_decoder_3_p3, bcd_to_7_segment_decoder_3_p4, bcd_to_7_segment_decoder_3_p6,
       bcd_to_7_segment_decoder_3_p7, bcd_to_7_segment_decoder_3_p8, bcd_to_7_segment_decoder_4_p1,
       bcd_to_7_segment_decoder_4_p2, bcd_to_7_segment_decoder_4_p3, bcd_to_7_segment_decoder_4_p4,
       bcd_to_7_segment_decoder_4_p6, bcd_to_7_segment_decoder_4_p7, bcd_to_7_segment_decoder_4_p8,
       clock_1_out, d_ff_1_q, d_ff_1_qn, d_ff_2_q, d_ff_2_qn, d_ff_3_q, d_ff_3_qn, d_ff_4_q, d_ff_4_qn,
       d_ff_5_q, d_ff_5_qn, d_ff_6_q, d_ff_6_qn, undriven;
  wire [2:0] counter_2_q, counter_4_q;
  wire [3:0] counter_1_q, counter_3_q;

  Clock clock_1 (.out(clock_1_out));
  D_Flip_Flop d_ff_1 (.D(d_ff_1_qn), .clk(undriven), .Q(d_ff_1_q), .Qn(d_ff_1_qn));  // open: preset, reset
  D_Flip_Flop d_ff_2 (.D(d_ff_2_qn), .clk(d_ff_1_q), .Q(d_ff_2_q), .Qn(d_ff_2_qn));  // open: preset, reset
  D_Flip_Flop d_ff_3 (.D(d_ff_3_qn), .clk(d_ff_2_q), .Q(d_ff_3_q), .Qn(d_ff_3_qn));  // open: preset, reset
  D_Flip_Flop d_ff_4 (.D(d_ff_4_qn), .clk(d_ff_3_q), .Q(d_ff_4_q), .Qn(d_ff_4_qn));  // open: preset, reset
  D_Flip_Flop d_ff_5 (.D(d_ff_5_qn), .clk(d_ff_4_q), .Q(d_ff_5_q), .Qn(d_ff_5_qn));  // open: preset, reset
  Counter #(.max('hf), .width(4)) counter_1 (
    .clr(in_1), .load(and_1_out), .count(1'b1), .clk(clock_1_out), .D({in_5, in_4, in_3, in_2}),
    .Q(counter_1_q));  // open: up, carry
  D_Flip_Flop d_ff_6 (.D(d_ff_6_qn), .clk(d_ff_5_q), .Q(d_ff_6_q), .Qn(d_ff_6_qn));  // open: preset, reset
  Counter #(.max('h7), .width(3)) counter_2 (
    .clr(in_6), .load(and_2_out), .count(and_1_out), .clk(clock_1_out), .D({in_9, in_8, in_7}),
    .Q(counter_2_q));  // open: up, carry
  Counter #(.max('hf), .width(4)) counter_3 (
    .clr(in_11), .load(and_4_out), .count(and_2_out), .clk(clock_1_out), .D({in_15, in_14, in_13, in_12}),
    .Q(counter_3_q));  // open: up, carry
  Counter #(.max('h7), .width(3)) counter_4 (
    .clr(in_16), .load(and_3_out), .count(and_4_out), .clk(clock_1_out), .D({in_19, in_18, in_17}),
    .Q(counter_4_q));  // open: up, carry
  and and_1 (and_1_out, counter_1_q[0], counter_1_q[3]);
  and and_2 (and_2_out, counter_2_q[0], and_1_out, counter_2_q[2]);
  and and_3 (and_3_out, counter_4_q[2], and_4_out, counter_4_q[0]);
  and and_4 (and_4_out, counter_3_q[3], and_2_out, counter_3_q[0]);
  // BCD_to_7_Segment_decoder bcd_to_7_segment_decoder_1: pin names not known; wires that end beside it: bcd_to_7_segment_decoder_1_p1, bcd_to_7_segment_decoder_1_p2, bcd_to_7_segment_decoder_1_p3, bcd_to_7_segment_decoder_1_p4, {in_10, counter_2_q}, bcd_to_7_segment_decoder_1_p6, bcd_to_7_segment_decoder_1_p7, bcd_to_7_segment_decoder_1_p8
  // BCD_to_7_Segment_decoder bcd_to_7_segment_decoder_2: pin names not known; wires that end beside it: bcd_to_7_segment_decoder_2_p1, bcd_to_7_segment_decoder_2_p2, bcd_to_7_segment_decoder_2_p3, bcd_to_7_segment_decoder_2_p4, {in_20, counter_4_q}, bcd_to_7_segment_decoder_2_p6, bcd_to_7_segment_decoder_2_p7, bcd_to_7_segment_decoder_2_p8
  // BCD_to_7_Segment_decoder bcd_to_7_segment_decoder_3: pin names not known; wires that end beside it: bcd_to_7_segment_decoder_3_p1, bcd_to_7_segment_decoder_3_p2, bcd_to_7_segment_decoder_3_p3, bcd_to_7_segment_decoder_3_p4, counter_1_q, bcd_to_7_segment_decoder_3_p6, bcd_to_7_segment_decoder_3_p7, bcd_to_7_segment_decoder_3_p8
  // BCD_to_7_Segment_decoder bcd_to_7_segment_decoder_4: pin names not known; wires that end beside it: bcd_to_7_segment_decoder_4_p1, bcd_to_7_segment_decoder_4_p2, bcd_to_7_segment_decoder_4_p3, bcd_to_7_segment_decoder_4_p4, counter_3_q, bcd_to_7_segment_decoder_4_p6, bcd_to_7_segment_decoder_4_p7, bcd_to_7_segment_decoder_4_p8
  _7_Segment_Display u_7_segment_display_1 (
    .g(bcd_to_7_segment_decoder_2_p1), .f(bcd_to_7_segment_decoder_2_p3), .a(bcd_to_7_segment_decoder_2_p6),
    .b(bcd_to_7_segment_decoder_2_p8), .e(bcd_to_7_segment_decoder_2_p2), .d(bcd_to_7_segment_decoder_2_p4),
    .c(bcd_to_7_segment_decoder_2_p7));  // open: dp
  _7_Segment_Display u_7_segment_display_2 (
    .g(bcd_to_7_segment_decoder_4_p1), .f(bcd_to_7_segment_decoder_4_p3), .a(bcd_to_7_segment_decoder_4_p6),
    .b(bcd_to_7_segment_decoder_4_p8), .e(bcd_to_7_segment_decoder_4_p2), .d(bcd_to_7_segment_decoder_4_p4),
    .c(bcd_to_7_segment_decoder_4_p7));  // open: dp
  _7_Segment_Display u_7_segment_display_3 (
    .g(bcd_to_7_segment_decoder_1_p1), .f(bcd_to_7_segment_decoder_1_p3), .a(bcd_to_7_segment_decoder_1_p6),
    .b(bcd_to_7_segment_decoder_1_p8), .e(bcd_to_7_segment_decoder_1_p2), .d(bcd_to_7_segment_decoder_1_p4),
    .c(bcd_to_7_segment_decoder_1_p7));  // open: dp
  _7_Segment_Display u_7_segment_display_4 (
    .g(bcd_to_7_segment_decoder_3_p1), .f(bcd_to_7_segment_decoder_3_p3), .a(bcd_to_7_segment_decoder_3_p6),
    .b(bcd_to_7_segment_decoder_3_p8), .e(bcd_to_7_segment_decoder_3_p2), .d(bcd_to_7_segment_decoder_3_p4),
    .c(bcd_to_7_segment_decoder_3_p7));  // open: dp
endmodule
