// Logisim project minutes_seconds2_final.circ as structural Verilog: 2 circuits, main circuit main
module main (
  input  in_1,
  input  in_2,
  input  in_3,
  input  in_4,
  input  in_5,
  input  BTNC,
  input  in_7,
  input  in_8,
  input  in_9,
  input  in_10,
  input  in_11,
  input  in_12,
  input  in_13,
  input  in_14,
  input  in_15,
  input  in_16,
  input  in_17,
  input  in_18,
  input  in_19,
  input  in_20,
  input  in_21,
  input  in_22,
  input  in_23,
  input  in_24,
  input  in_25,
  input  in_26,
  input  in_27,
  input  in_28,
  input  in_29,
  input  in_30,
  input  in_31
);

  wire and_1_out, and_2_out, and_3_out, and_4_out, and_5_out, and_6_out, and_7_out, and_8_out,
       bcd_to_7_segment_decoder_1_p1, bcd_to_7_segment_decoder_1_p2, bcd_to_7_segment_decoder_1_p3,
       bcd_to_7_segment_decoder_1_p4, bcd_to_7_segment_decoder_1_p6, bcd_to_7_segment_decoder_1_p7,
       bcd_to_7_segment_decoder_1_p8, bcd_to_7_segment_decoder_2_p1, bcd_to_7_segment_decoder_2_p2,
       bcd_to_7_segment_decoder_2_p3, bcd_to_7_segment_decoder_2_p4, bcd_to_7_segment_decoder_2_p6,
       bcd_to_7_segment_decoder_2_p7, bcd_to_7_segment_decoder_2_p8, bcd_to_7_segment_decoder_3_p1,
       bcd_to_7_segment_decoder_3_p2, bcd_to_7_segment_decoder_3_p3, bcd_to_7_segment_decoder_3_p4,
       bcd_to_7_segment_decoder_3_p6, bcd_to_7_segment_decoder_3_p7, bcd_to_7_segment_decoder_3_p8,
       bcd_to_7_segment_decoder_4_p1, bcd_to_7_segment_decoder_4_p2, bcd_to_7_segment_decoder_4_p3,
       bcd_to_7_segment_decoder_4_p4, bcd_to_7_segment_decoder_4_p6, bcd_to_7_segment_decoder_4_p7,
       bcd_to_7_segment_decoder_4_p8, bcd_to_7_segment_decoder_5_p1, bcd_to_7_segment_decoder_5_p2,
       bcd_to_7_segment_decoder_5_p3, bcd_to_7_segment_decoder_5_p4, bcd_to_7_segment_decoder_5_p6,
       bcd_to_7_segment_decoder_5_p7, bcd_to_7_segment_decoder_5_p8, bcd_to_7_segment_decoder_6_p1,
       bcd_to_7_segment_decoder_6_p2, bcd_to_7_segment_decoder_6_p3, bcd_to_7_segment_decoder_6_p4,
       bcd_to_7_segment_decoder_6_p6, bcd_to_7_segment_decoder_6_p7, bcd_to_7_segment_decoder_6_p8, BTND_out,
       BTNL_out, BTNR_out, BTNU_out, clock_1_out, counter_2_carry, not_1_out, or_1_out, or_2_out;
  wire [1:0] adjust_1_mux_out;
  wire [2:0] counter_3_q, counter_5_q, counter_6_q;
  wire [3:0] adjust_1_alarm_hour_1, adjust_1_alarm_hour_2, adjust_1_alarm_min_1, adjust_1_alarm_min_2,
       adjust_1_time_hour_1, adjust_1_time_hour_2, adjust_1_time_min_1, adjust_1_time_min_2,
       bcd_to_7_segment_decoder_2_p5, bcd_to_7_segment_decoder_3_p5, bcd_to_7_segment_decoder_6_p5,
       counter_1_q, counter_2_q, counter_4_q, multiplexer_2_out, multiplexer_3_out, multiplexer_4_out,
       multiplexer_6_out, multiplexer_8_out;
  wire [6:0] adjust_1_out_6;

  Clock clock_1 (.out(clock_1_out));
  Button BTNL (.out(BTNL_out));
  Button BTNR (.out(BTNR_out));
  Button BTND (.out(BTND_out));
  Button BTNU (.out(BTNU_out));
  not not_1 (not_1_out, BTNC);
  and and_1 (and_1_out, clock_1_out, not_1_out);
  or or_1 (or_1_out, and_2_out, and_6_out);
  or or_2 (or_2_out, and_2_out, and_5_out);
  Counter #(.max('hf), .width(4)) counter_1 (
    .clr(in_1), .load(and_3_out), .count(1'b1), .clk(and_1_out), .D({in_5, in_4, in_3, in_2}), .Q(counter_1_q));  // open: up, carry
  Counter #(.max('hf), .width(4)) counter_2 (
    .clr(in_22), .load(or_2_out), .count(and_7_out), .clk(and_1_out), .D({in_26, in_25, in_24, in_23}),
    .carry(counter_2_carry), .Q(counter_2_q));  // open: up
  Counter #(.max('h7), .width(3)) counter_3 (
    .clr(in_7), .load(and_4_out), .count(and_3_out), .clk(and_1_out), .D({in_10, in_9, in_8}), .Q(counter_3_q));  // open: up, carry
  Counter #(.max('hf), .width(4)) counter_4 (
    .clr(in_12), .load(and_8_out), .count(and_4_out), .clk(and_1_out), .D({in_16, in_15, in_14, in_13}),
    .Q(counter_4_q));  // open: up, carry
  Counter #(.max('h7), .width(3)) counter_5 (
    .clr(in_17), .load(and_7_out), .count(and_8_out), .clk(and_1_out), .D({in_20, in_19, in_18}),
    .Q(counter_5_q));  // open: up, carry
  Counter #(.max('h7), .width(3)) counter_6 (
    .clr(in_27), .load(or_1_out), .count(and_5_out), .clk(and_1_out), .D({in_30, in_29, in_28}),
    .Q(counter_6_q));  // open: up, carry
  and and_2 (and_2_out, counter_2_q[2], counter_6_q[1]);
  Adjust adjust_1 (
    .BTNL(BTNL_out), .BTNR(BTNR_out), .BTND(BTND_out), .BTNU(BTNU_out), .mux_out(adjust_1_mux_out),
    .out_6(adjust_1_out_6), .Time_min_1(adjust_1_time_min_1), .Time_min_2(adjust_1_time_min_2),
    .Time_Hour_1(adjust_1_time_hour_1), .Time_Hour_2(adjust_1_time_hour_2),
    .Alarm_min_1(adjust_1_alarm_min_1), .Alarm_min_2(adjust_1_alarm_min_2),
    .Alarm_Hour_1(adjust_1_alarm_hour_1), .Alarm_Hour_2(adjust_1_alarm_hour_2));  // open: out_7, out_10, out_11, out_14, out_15, out_18, out_19
  and and_3 (and_3_out, counter_1_q[0], counter_1_q[3]);
  and and_4 (and_4_out, counter_3_q[0], and_3_out, counter_3_q[2]);
  and and_5 (and_5_out, counter_2_q[0], and_7_out, counter_2_q[3]);
  and and_6 (and_6_out, counter_6_q[1], and_5_out);
  and and_7 (and_7_out, counter_5_q[2], and_8_out, counter_5_q[0]);
  and and_8 (and_8_out, counter_4_q[3], and_4_out, counter_4_q[0]);
  // BCD_to_7_Segment_decoder bcd_to_7_segment_decoder_1: pin names not known; wires that end beside it: bcd_to_7_segment_decoder_1_p1, bcd_to_7_segment_decoder_1_p2, bcd_to_7_segment_decoder_1_p3, bcd_to_7_segment_decoder_1_p4, {in_11, counter_3_q}, bcd_to_7_segment_decoder_1_p6, bcd_to_7_segment_decoder_1_p7, bcd_to_7_segment_decoder_1_p8
  // BCD_to_7_Segment_decoder bcd_to_7_segment_decoder_2: pin names not known; wires that end beside it: bcd_to_7_segment_decoder_2_p1, bcd_to_7_segment_decoder_2_p2, bcd_to_7_segment_decoder_2_p3, bcd_to_7_segment_decoder_2_p4, bcd_to_7_segment_decoder_2_p5, bcd_to_7_segment_decoder_2_p6, bcd_to_7_segment_decoder_2_p7, bcd_to_7_segment_decoder_2_p8
  Multiplexer #(.width(4)) multiplexer_1 (
    .in0({in_31, counter_6_q}), .in1(multiplexer_8_out), .out(bcd_to_7_segment_decoder_2_p5), .sel(BTNC));
  Multiplexer #(.width(4)) multiplexer_2 (
    .in0(adjust_1_time_min_1), .in1(adjust_1_alarm_min_1), .out(multiplexer_2_out), .sel(adjust_1_mux_out[1]));
  Multiplexer #(.width(4)) multiplexer_3 (
    .in0(counter_4_q), .in1(multiplexer_2_out), .out(multiplexer_3_out), .sel(BTNC));
  Multiplexer #(.width(4)) multiplexer_4 (
    .in0(adjust_1_time_min_2), .in1(adjust_1_alarm_min_2), .out(multiplexer_4_out), .sel(adjust_1_mux_out[1]));
  // BCD_to_7_Segment_decoder bcd_to_7_segment_decoder_3: pin names not known; wires that end beside it: bcd_to_7_segment_decoder_3_p1, bcd_to_7_segment_decoder_3_p2, bcd_to_7_segment_decoder_3_p3, bcd_to_7_segment_decoder_3_p4, bcd_to_7_segment_decoder_3_p5, bcd_to_7_segment_decoder_3_p6, bcd_to_7_segment_decoder_3_p7, bcd_to_7_segment_decoder_3_p8
  Multiplexer #(.width(4)) multiplexer_5 (
    .in0({in_21, counter_5_q}), .in1(multiplexer_4_out), .out(bcd_to_7_segment_decoder_3_p5), .sel(BTNC));
  Multiplexer #(.width(4)) multiplexer_6 (
    .in0(adjust_1_time_hour_1), .in1(adjust_1_alarm_hour_1), .out(multiplexer_6_out),
    .sel(adjust_1_mux_out[1]));
  // BCD_to_7_Segment_decoder bcd_to_7_segment_decoder_4: pin names not known; wires that end beside it: bcd_to_7_segment_decoder_4_p1, bcd_to_7_segment_decoder_4_p2, bcd_to_7_segment_decoder_4_p3, bcd_to_7_segment_decoder_4_p4, counter_1_q, bcd_to_7_segment_decoder_4_p6, bcd_to_7_segment_decoder_4_p7, bcd_to_7_segment_decoder_4_p8
  // BCD_to_7_Segment_decoder bcd_to_7_segment_decoder_5: pin names not known; wires that end beside it: bcd_to_7_segment_decoder_5_p1, bcd_to_7_segment_decoder_5_p2, bcd_to_7_segment_decoder_5_p3, bcd_to_7_segment_decoder_5_p4, multiplexer_3_out, bcd_to_7_segment_decoder_5_p6, bcd_to_7_segment_decoder_5_p7, bcd_to_7_segment_decoder_5_p8
  // BCD_to_7_Segment_decoder bcd_to_7_segment_decoder_6: pin names not known; wires that end beside it: bcd_to_7_segment_decoder_6_p1, bcd_to_7_segment_decoder_6_p2, bcd_to_7_segment_decoder_6_p3, bcd_to_7_segment_decoder_6_p4, bcd_to_7_segment_decoder_6_p5, bcd_to_7_segment_decoder_6_p6, bcd_to_7_segment_decoder_6_p7, bcd_to_7_segment_decoder_6_p8
  Multiplexer #(.width(4)) multiplexer_7 (
    .in0(counter_2_q), .in1(multiplexer_6_out), .out(bcd_to_7_segment_decoder_6_p5), .sel(BTNC));
  Multiplexer #(.width(4)) multiplexer_8 (
    .in0(adjust_1_time_hour_2), .in1(adjust_1_alarm_hour_2), .out(multiplexer_8_out),
    .sel(adjust_1_mux_out[1]));
  _7_Segment_Display u_7_segment_display_1 (
    .g(bcd_to_7_segment_decoder_3_p1), .f(bcd_to_7_segment_decoder_3_p3), .a(bcd_to_7_segment_decoder_3_p6),
    .b(bcd_to_7_segment_decoder_3_p8), .e(bcd_to_7_segment_decoder_3_p2), .d(bcd_to_7_segment_decoder_3_p4),
    .c(bcd_to_7_segment_decoder_3_p7));  // open: dp
  _7_Segment_Display u_7_segment_display_2 (
    .g(bcd_to_7_segment_decoder_2_p1), .f(bcd_to_7_segment_decoder_2_p3), .a(bcd_to_7_segment_decoder_2_p6),
    .b(bcd_to_7_segment_decoder_2_p8), .e(bcd_to_7_segment_decoder_2_p2), .d(bcd_to_7_segment_decoder_2_p4),
    .c(bcd_to_7_segment_decoder_2_p7));  // open: dp
  _7_Segment_Display u_7_segment_display_3 (
    .g(bcd_to_7_segment_decoder_5_p1), .f(bcd_to_7_segment_decoder_5_p3), .a(bcd_to_7_segment_decoder_5_p6),
    .b(bcd_to_7_segment_decoder_5_p8), .e(bcd_to_7_segment_decoder_5_p2), .d(bcd_to_7_segment_decoder_5_p4),
    .c(bcd_to_7_segment_decoder_5_p7));  // open: dp
  _7_Segment_Display u_7_segment_display_4 (
    .g(bcd_to_7_segment_decoder_6_p1), .f(bcd_to_7_segment_decoder_6_p3), .a(bcd_to_7_segment_decoder_6_p6),
    .b(bcd_to_7_segment_decoder_6_p8), .e(bcd_to_7_segment_decoder_6_p2), .d(bcd_to_7_segment_decoder_6_p4),
    .c(bcd_to_7_segment_decoder_6_p7));  // open: dp
  _7_Segment_Display u_7_segment_display_5 (
    .g(bcd_to_7_segment_decoder_1_p1), .f(bcd_to_7_segment_decoder_1_p3), .a(bcd_to_7_segment_decoder_1_p6),
    .b(bcd_to_7_segment_decoder_1_p8), .e(bcd_to_7_segment_decoder_1_p2), .d(bcd_to_7_segment_decoder_1_p4),
    .c(bcd_to_7_segment_decoder_1_p7));  // open: dp
  _7_Segment_Display u_7_segment_display_6 (
    .g(bcd_to_7_segment_decoder_4_p1), .f(bcd_to_7_segment_decoder_4_p3), .a(bcd_to_7_segment_decoder_4_p6),
    .b(bcd_to_7_segment_decoder_4_p8), .e(bcd_to_7_segment_decoder_4_p2), .d(bcd_to_7_segment_decoder_4_p4),
    .c(bcd_to_7_segment_decoder_4_p7));  // open: dp
endmodule

module Adjust (
  input  BTNL,
  input  BTNR,
  input  BTND,
  input  BTNU,
  output [1:0] mux_out,
  output [6:0] out_6,
  output [6:0] out_7,
  output [3:0] Time_min_1,
  output [3:0] Time_min_2,
  output [6:0] out_10,
  output [6:0] out_11,
  output [3:0] Time_Hour_1,
  output [3:0] Time_Hour_2,
  output [6:0] out_14,
  output [6:0] out_15,
  output [3:0] Alarm_min_1,
  output [3:0] Alarm_min_2,
  output [6:0] out_18,
  output [6:0] out_19,
  output [3:0] Alarm_Hour_1,
  output [3:0] Alarm_Hour_2
);

  wire and_1_out, and_2_out, and_3_out, and_4_out, and_5_out, and_6_out, and_7_out, and_8_out, and_9_out,
       and_10_out, and_11_out, and_12_out, and_13_out, and_14_out, bcd_to_7_segment_decoder_3_p5,
       counter_6_carry, counter_8_carry, decoder_1_out0, decoder_1_out1, decoder_1_out2, decoder_1_out3,
       or_1_out, or_2_out, or_3_out, or_4_out;

  or or_1 (or_1_out, BTNL, BTNR);
  or or_2 (or_2_out, BTND, BTNU);
  Decoder #(.enable("false"), .select(2)) decoder_1 (
    .out0(decoder_1_out0), .out1(decoder_1_out1), .out2(decoder_1_out2), .out3(decoder_1_out3), .sel(mux_out));
  Counter #(.max('h3), .width(2)) counter_1 (
    .clr(1'b0), .up(BTNR), .clk(or_1_out), .D(2'b00), .Q(mux_out));  // open: load, count, carry
  and and_1 (and_1_out, decoder_1_out2, or_2_out);
  and and_2 (and_2_out, decoder_1_out1, BTNU);
  and and_3 (and_3_out, decoder_1_out1, or_2_out);
  and and_4 (and_4_out, decoder_1_out3, BTNU);
  and and_5 (and_5_out, decoder_1_out3, or_2_out);
  and and_6 (and_6_out, decoder_1_out2, BTNU);
  and and_7 (and_7_out, decoder_1_out0, BTNU);
  and and_8 (and_8_out, decoder_1_out0, or_2_out);
  Counter #(.max('h9), .width(4)) counter_2 (
    .clr(1'b0), .load(1'b0), .up(and_2_out), .count(1'b1), .clk(and_3_out), .Q(Time_min_1));  // open: D, carry
  Counter #(.max('h5), .width(3)) counter_3 (
    .clr(1'b0), .up(and_2_out), .count(and_10_out), .clk(and_3_out), .Q(Time_min_2[2:0]));  // open: load, D, carry
  Counter #(.max('h9), .width(4)) counter_4 (
    .clr(1'b0), .load(1'b0), .up(and_4_out), .count(1'b1), .clk(and_5_out), .Q(Alarm_min_1));  // open: D, carry
  Counter #(.max('h5), .width(3)) counter_5 (
    .clr(1'b0), .up(and_4_out), .count(and_11_out), .clk(and_5_out), .Q(Alarm_min_2[2:0]));  // open: load, D, carry
  Counter #(.max('h9), .width(4)) counter_6 (
    .clr(1'b0), .load(and_9_out), .up(and_6_out), .count(1'b1), .clk(and_1_out), .D(4'b0000),
    .carry(counter_6_carry), .Q(Alarm_Hour_1));
  Counter #(.max('h2), .width(3)) counter_7 (
    .clr(1'b0), .up(and_6_out), .count(or_3_out), .clk(and_1_out), .Q(Alarm_Hour_2[2:0]));  // open: load, D, carry
  or or_3 (or_3_out, and_9_out, and_12_out);
  Counter #(.max('h9), .width(4)) counter_8 (
    .clr(1'b0), .load(and_13_out), .up(and_7_out), .count(1'b1), .clk(and_8_out), .D(4'b0000),
    .carry(counter_8_carry), .Q(Time_Hour_1));
  Counter #(.max('h2), .width(3)) counter_9 (
    .clr(1'b0), .up(and_7_out), .count(or_4_out), .clk(and_8_out), .Q(Time_Hour_2[2:0]));  // open: load, D, carry
  and and_9 (and_9_out, Alarm_Hour_2[1], Alarm_Hour_1[0], Alarm_Hour_1[1]);
  and and_10 (and_10_out, Time_min_1[3], Time_min_1[0]);
  or or_4 (or_4_out, and_13_out, and_14_out);
  and and_11 (and_11_out, Alarm_min_1[3], Alarm_min_1[0]);
  and and_12 (and_12_out, Alarm_Hour_1[3], Alarm_Hour_1[0]);
  and and_13 (and_13_out, Time_Hour_2[1], Time_Hour_1[0], Time_Hour_1[1]);
  // BCD_to_7_Segment_decoder bcd_to_7_segment_decoder_1: pin names not known; wires that end beside it: out_18[0], out_18[4], out_18[1], out_18[5], out_18[2], out_18[6], out_18[3]
  and and_14 (and_14_out, Time_Hour_1[3], Time_Hour_1[0]);
  // BCD_to_7_Segment_decoder bcd_to_7_segment_decoder_2: pin names not known; wires that end beside it: out_14[0], out_14[4], out_14[1], out_14[5], out_14[2], out_14[6], out_14[3]
  // BCD_to_7_Segment_decoder bcd_to_7_segment_decoder_3: pin names not known; wires that end beside it: out_6[0], out_6[4], out_6[1], out_6[5], bcd_to_7_segment_decoder_3_p5, bcd_to_7_segment_decoder_3_p5, out_6[2], out_6[6], out_6[3]
  // BCD_to_7_Segment_decoder bcd_to_7_segment_decoder_4: pin names not known; wires that end beside it: counter_8_carry, out_10[0], out_10[4], out_10[1], out_10[5], out_10[2], out_10[6], out_10[3]
  // BCD_to_7_Segment_decoder bcd_to_7_segment_decoder_5: pin names not known; wires that end beside it: out_19[0], out_19[4], out_19[1], out_19[5], out_19[2], out_19[6], out_19[3]
  // BCD_to_7_Segment_decoder bcd_to_7_segment_decoder_6: pin names not known; wires that end beside it: out_7[0], out_7[4], out_7[1], out_7[5], out_7[2], out_7[6], out_7[3]
  // BCD_to_7_Segment_decoder bcd_to_7_segment_decoder_7: pin names not known; wires that end beside it: out_11[0], out_11[4], out_11[1], out_11[5], out_11[2], out_11[6], out_11[3]
  // BCD_to_7_Segment_decoder bcd_to_7_segment_decoder_8: pin names not known; wires that end beside it: out_15[0], out_15[4], out_15[1], out_15[5], out_15[2], out_15[6], out_15[3]

  assign Alarm_Hour_2[3] = 1'b0;
  assign Alarm_min_2[3] = 1'b0;
  assign Time_Hour_2[3] = 1'b0;
  assign Time_min_2[3] = 1'b0;
endmodule
